// Logisim project Contadores Sincronos.circ as structural Verilog: 3 circuits, main circuit main
module main (
  input  in_1
);

  wire clock_1_out, n0_a_9_1_j0, n0_a_9_1_j1, n0_a_9_1_j2, n0_a_9_1_j3, n0_a_9_1_k0, n0_a_9_1_k1,
       n0_a_9_1_k2, n0_a_9_1_k3;
  wire [3:0] j_k_ff_4_q;

  Clock clock_1 (.out(clock_1_out));
  J_K_Flip_Flop j_k_ff_1 (
    .J(n0_a_9_1_j3), .clk(clock_1_out), .K(n0_a_9_1_k3), .Q(j_k_ff_4_q[3]), .reset(in_1));  // open: Qn, preset, en
  J_K_Flip_Flop j_k_ff_2 (
    .J(n0_a_9_1_k2), .clk(clock_1_out), .K(n0_a_9_1_j2), .Q(j_k_ff_4_q[2]), .reset(in_1));  // open: Qn, preset, en
  J_K_Flip_Flop j_k_ff_3 (
    .J(n0_a_9_1_j1), .clk(clock_1_out), .K(n0_a_9_1_k1), .Q(j_k_ff_4_q[1]), .reset(in_1));  // open: Qn, preset, en
  J_K_Flip_Flop j_k_ff_4 (
    .J(n0_a_9_1_j0), .clk(clock_1_out), .K(n0_a_9_1_k0), .Q(j_k_ff_4_q[0]), .reset(in_1));  // open: Qn, preset, en
  _0_a_9 u_0_a_9_1 (
    .Q3(j_k_ff_4_q[3]), .Q2(j_k_ff_4_q[2]), .Q1(j_k_ff_4_q[1]), .Q0(j_k_ff_4_q[0]), .J3(n0_a_9_1_j3),
    .K3(n0_a_9_1_k3), .J2(n0_a_9_1_j2), .K2(n0_a_9_1_k2), .J1(n0_a_9_1_j1), .K1(n0_a_9_1_k1),
    .J0(n0_a_9_1_j0), .K0(n0_a_9_1_k0));
  Hex_Digit_Display hex_digit_display_1 (.value(j_k_ff_4_q));  // open: dp
endmodule

module _0_a_F (
  input  Q3,
  input  Q2,
  input  Q1,
  input  Q0,
  output J3,
  output K3,
  output J2,
  output K2,
  output J1,
  output K1,
  output J0,
  output K0
);

  wire and_1_out;

  and and_1 (and_1_out, Q2, Q1, Q0);
  and and_2 (K3, Q2, Q1, Q0);
  and and_3 (J2, Q1, Q0);
  and and_4 (K2, Q1, Q0);
  or or_1 (J3, and_1_out, Q3);

  assign J0 = 1'b1;
  assign J1 = Q0;
  assign K0 = 1'b1;
  assign K1 = Q0;
endmodule

module _0_a_9 (
  input  Q3,
  input  Q2,
  input  Q1,
  input  Q0,
  output J3,
  output K3,
  output J2,
  output K2,
  output J1,
  output K1,
  output J0,
  output K0
);

  wire not_1_out;

  and and_1 (J3, Q2, Q1, Q0);
  and and_2 (J2, Q1, Q0);
  and and_3 (K2, Q1, Q0);
  not not_1 (not_1_out, Q3);
  and and_4 (J1, not_1_out, Q0);

  assign J0 = 1'b1;
  assign K0 = 1'b1;
  assign K1 = Q0;
  assign K3 = Q0;
endmodule
