// Logisim project NFF.circ as structural Verilog: 4 circuits, main circuit main
module main (
  input  Clear
);

  wire clock_1_out, jk_prclr_1_q, jk_prclr_2_q, jk_prclr_3_q, jk_prclr_4_q, n0af_1_j0, n0af_1_j1, n0af_1_j2,
       n0af_1_j3, n0af_1_k0, n0af_1_k1, n0af_1_k2, n0af_1_k3, n7seg_1_a, n7seg_1_b, n7seg_1_c, n7seg_1_d,
       n7seg_1_e, n7seg_1_f, n7seg_1_g;

  Clock clock_1 (.out(clock_1_out));
  JK_PRCLR jk_prclr_1 (
    .J(n0af_1_j3), .Clock(clock_1_out), .K(n0af_1_k3), .Q(jk_prclr_1_q), .PR(1'b1), .CLR(Clear));  // open: nQ
  JK_PRCLR jk_prclr_2 (
    .J(n0af_1_j2), .Clock(clock_1_out), .K(n0af_1_k2), .Q(jk_prclr_2_q), .PR(1'b1), .CLR(Clear));  // open: nQ
  JK_PRCLR jk_prclr_3 (
    .J(n0af_1_j1), .Clock(clock_1_out), .K(n0af_1_k1), .Q(jk_prclr_3_q), .PR(1'b1), .CLR(Clear));  // open: nQ
  JK_PRCLR jk_prclr_4 (
    .J(n0af_1_j0), .Clock(clock_1_out), .K(n0af_1_k0), .Q(jk_prclr_4_q), .PR(1'b1), .CLR(Clear));  // open: nQ
  _0aF u_0af_1 (
    .Q3(jk_prclr_1_q), .Q2(jk_prclr_2_q), .Q1(jk_prclr_3_q), .Q0(jk_prclr_4_q), .J3(n0af_1_j3),
    .K3(n0af_1_k3), .J2(n0af_1_j2), .K2(n0af_1_k2), .J1(n0af_1_j1), .K1(n0af_1_k1), .J0(n0af_1_j0),
    .K0(n0af_1_k0));
  _7seg u_7seg_1 (
    .Q3(jk_prclr_1_q), .Q2(jk_prclr_2_q), .Q1(jk_prclr_3_q), .Q0(jk_prclr_4_q), .a(n7seg_1_a), .b(n7seg_1_b),
    .c(n7seg_1_c), .d(n7seg_1_d), .e(n7seg_1_e), .f(n7seg_1_f), .g(n7seg_1_g));
  _7_Segment_Display u_7_segment_display_1 (
    .g(n7seg_1_g), .f(n7seg_1_f), .a(n7seg_1_a), .b(n7seg_1_b), .e(n7seg_1_e), .d(n7seg_1_d), .c(n7seg_1_c));  // open: dp

  // Notes on the sheet:
  //   na primeira execução, usar o clear pra começar a funcionar
endmodule

module _7seg (
  input  Q3,
  input  Q2,
  input  Q1,
  input  Q0,
  output a,
  output b,
  output c,
  output d,
  output e,
  output f,
  output g
);

  wire and_1_out, and_2_out, and_3_out, and_4_out, and_5_out, and_6_out, and_7_out, and_8_out, and_9_out,
       and_10_out, and_11_out, and_12_out, and_13_out, and_14_out, and_15_out, and_16_out, and_17_out,
       and_18_out, and_19_out, and_20_out, and_21_out, and_22_out, and_23_out, and_24_out, and_25_out,
       and_26_out, and_27_out, and_28_out, and_29_out, and_30_out, and_31_out, and_32_out, and_33_out,
       and_34_out, and_35_out, and_36_out, and_37_out, and_38_out, and_39_out, and_40_out, and_41_out,
       and_42_out, and_43_out, and_44_out, and_45_out, and_46_out, not_1_out, not_2_out, not_3_out,
       not_4_out, not_5_out, not_6_out, not_7_out, not_8_out, not_9_out, not_10_out, not_11_out, not_12_out,
       not_13_out, not_14_out, not_15_out, not_16_out, not_17_out, not_18_out, not_19_out, not_20_out,
       not_21_out, not_22_out, not_23_out, not_24_out, not_25_out, not_26_out, not_27_out, not_28_out,
       not_29_out, not_30_out, not_31_out, not_32_out, not_33_out, not_34_out, not_35_out, not_36_out,
       not_37_out, not_38_out, not_39_out, not_40_out, not_41_out, not_42_out, not_43_out, or_1_out,
       or_2_out, or_3_out, or_4_out, or_5_out, or_6_out, or_7_out, or_8_out, or_9_out, or_10_out, or_12_out,
       or_13_out, or_14_out, or_15_out, or_16_out, or_17_out, or_18_out, or_20_out, or_21_out, or_22_out,
       or_23_out;

  not not_1 (not_1_out, Q2);
  not not_2 (not_2_out, Q0);
  not not_3 (not_3_out, Q3);
  not not_4 (not_4_out, Q3);
  and and_1 (and_1_out, Q3, not_5_out);
  not not_5 (not_5_out, Q2);
  not not_6 (not_6_out, Q1);
  not not_7 (not_7_out, Q3);
  not not_8 (not_8_out, Q2);
  not not_9 (not_9_out, Q3);
  and and_2 (and_2_out, not_9_out, not_10_out);
  not not_10 (not_10_out, Q1);
  not not_11 (not_11_out, Q0);
  not not_12 (not_12_out, Q3);
  not not_13 (not_13_out, Q1);
  not not_14 (not_14_out, Q3);
  and and_3 (and_3_out, not_14_out, not_15_out);
  not not_15 (not_15_out, Q1);
  not not_16 (not_16_out, Q3);
  and and_4 (and_4_out, not_16_out, Q0);
  not not_17 (not_17_out, Q1);
  not not_18 (not_18_out, Q3);
  not not_19 (not_19_out, Q2);
  not not_20 (not_20_out, Q3);
  and and_5 (and_5_out, not_20_out, not_21_out);
  not not_21 (not_21_out, Q2);
  not not_22 (not_22_out, Q0);
  not not_23 (not_23_out, Q2);
  and and_6 (and_6_out, not_23_out, Q1);
  not not_24 (not_24_out, Q1);
  not not_25 (not_25_out, Q2);
  and and_7 (and_7_out, not_25_out, not_26_out);
  not not_26 (not_26_out, Q0);
  and and_8 (and_8_out, Q1, not_27_out);
  not not_27 (not_27_out, Q0);
  and and_9 (and_9_out, Q3, Q1);
  and and_10 (and_10_out, Q3, Q2);
  not not_28 (not_28_out, Q1);
  not not_29 (not_29_out, Q0);
  not not_30 (not_30_out, Q3);
  and and_11 (and_11_out, not_30_out, Q2);
  not not_31 (not_31_out, Q1);
  not not_32 (not_32_out, Q2);
  and and_12 (and_12_out, not_32_out, Q1);
  and and_13 (and_13_out, Q1, not_33_out);
  not not_33 (not_33_out, Q0);
  not not_34 (not_34_out, Q3);
  and and_14 (and_14_out, not_34_out, Q2);
  not not_35 (not_35_out, Q1);
  not not_36 (not_36_out, Q2);
  and and_15 (and_15_out, not_1_out, not_2_out);
  and and_16 (and_16_out, not_3_out, Q1);
  and and_17 (and_17_out, not_4_out, Q2);
  and and_18 (and_18_out, Q2, Q1);
  and and_19 (and_19_out, and_1_out, not_6_out);
  not not_37 (not_37_out, Q0);
  and and_20 (and_20_out, not_7_out, not_8_out);
  and and_21 (and_21_out, and_2_out, not_11_out);
  not not_38 (not_38_out, Q2);
  not not_39 (not_39_out, Q0);
  and and_22 (and_22_out, not_12_out, Q1);
  and and_23 (and_23_out, Q3, not_13_out);
  or or_1 (or_1_out, and_3_out, and_4_out);
  and and_24 (and_24_out, not_17_out, Q0);
  and and_25 (and_25_out, not_18_out, Q2);
  and and_26 (and_26_out, Q3, not_19_out);
  and and_27 (and_27_out, and_5_out, not_22_out);
  and and_28 (and_28_out, and_6_out, Q0);
  and and_29 (and_29_out, Q2, not_24_out);
  and and_30 (and_30_out, Q2, Q1);
  not not_40 (not_40_out, Q0);
  not not_41 (not_41_out, Q1);
  or or_2 (or_2_out, and_7_out, and_8_out);
  or or_3 (or_3_out, and_9_out, and_10_out);
  and and_31 (and_31_out, not_28_out, not_29_out);
  and and_32 (and_32_out, and_11_out, not_31_out);
  not not_42 (not_42_out, Q0);
  not not_43 (not_43_out, Q2);
  or or_4 (or_4_out, and_12_out, and_13_out);
  and and_33 (and_33_out, and_14_out, not_35_out);
  and and_34 (and_34_out, Q3, not_36_out);
  and and_35 (and_35_out, Q3, Q0);
  or or_5 (or_5_out, and_15_out, and_16_out);
  and and_36 (and_36_out, and_17_out, Q0);
  or or_6 (or_6_out, and_18_out, and_19_out);
  and and_37 (and_37_out, Q3, not_37_out);
  or or_7 (or_7_out, and_20_out, and_21_out);
  and and_38 (and_38_out, not_38_out, not_39_out);
  and and_39 (and_39_out, and_22_out, Q0);
  and and_40 (and_40_out, and_23_out, Q0);
  or or_8 (or_8_out, or_1_out, and_24_out);
  or or_9 (or_9_out, and_25_out, and_26_out);
  or or_10 (or_10_out, and_27_out, and_28_out);
  and and_41 (and_41_out, and_29_out, Q0);
  and and_42 (and_42_out, and_30_out, not_40_out);
  and and_43 (and_43_out, Q3, not_41_out);
  or or_11 (e, or_2_out, or_3_out);
  or or_12 (or_12_out, and_31_out, and_32_out);
  and and_44 (and_44_out, Q2, not_42_out);
  and and_45 (and_45_out, Q3, not_43_out);
  and and_46 (and_46_out, Q3, Q1);
  or or_13 (or_13_out, or_4_out, and_33_out);
  or or_14 (or_14_out, and_34_out, and_35_out);
  or or_15 (or_15_out, or_5_out, and_36_out);
  or or_16 (or_16_out, or_6_out, and_37_out);
  or or_17 (or_17_out, or_7_out, and_38_out);
  or or_18 (or_18_out, and_39_out, and_40_out);
  or or_19 (c, or_8_out, or_9_out);
  or or_20 (or_20_out, or_10_out, and_41_out);
  or or_21 (or_21_out, and_42_out, and_43_out);
  or or_22 (or_22_out, or_12_out, and_44_out);
  or or_23 (or_23_out, and_45_out, and_46_out);
  or or_24 (g, or_13_out, or_14_out);
  or or_25 (a, or_15_out, or_16_out);
  or or_26 (b, or_17_out, or_18_out);
  or or_27 (d, or_20_out, or_21_out);
  or or_28 (f, or_22_out, or_23_out);
endmodule

module _0aF (
  input  Q3,
  input  Q2,
  input  Q1,
  input  Q0,
  output J3,
  output K3,
  output J2,
  output K2,
  output J1,
  output K1,
  output J0,
  output K0
);

  and and_1 (J3, Q2, Q1, Q0);
  and and_2 (K3, Q2, Q1, Q0);
  and and_3 (J2, Q1, Q0);
  and and_4 (K2, Q1, Q0);

  assign J0 = 1'b1;
  assign J1 = Q0;
  assign K0 = 1'b1;
  assign K1 = Q0;
endmodule

module JK_PRCLR (
  input  PR,
  input  J,
  input  Clock,
  input  K,
  input  CLR,
  output Q,
  output nQ
);

  wire and_1_out, and_2_out, and_3_out, and_4_out, and_5_out, and_6_out, nand_1_out, nand_2_out, nand_3_out,
       nand_4_out, nand_5_out, nand_6_out, not_1_out, not_2_out;

  and and_1 (and_1_out, J, Clock);
  and and_2 (and_2_out, Clock, K);
  nand nand_1 (nand_1_out, and_1_out, nQ);
  and and_3 (and_3_out, nand_3_out, nand_2_out);
  nand nand_2 (nand_2_out, Q, and_2_out);
  nand nand_3 (nand_3_out, PR, and_4_out);
  and and_4 (and_4_out, nand_1_out, nand_4_out);
  not not_1 (not_1_out, Clock);
  nand nand_4 (nand_4_out, and_3_out, not_2_out);
  not not_2 (not_2_out, CLR);
  nand nand_5 (nand_5_out, nand_3_out, not_1_out);
  nand nand_6 (nand_6_out, not_1_out, nand_4_out);
  and and_5 (and_5_out, PR, nand_5_out);
  and and_6 (and_6_out, nand_6_out, not_2_out);
  nand nand_7 (Q, and_5_out, nQ);
  nand nand_8 (nQ, Q, and_6_out);

  // Notes on the sheet:
  //   Q1
  //   ~Q1
  //   Set
  //   Reset
  //   Primeiro NAND
endmodule
