// Logisim project Tarefa 03 - lab.circ as structural Verilog
module FLIP_FLOP_JK_PRCLR_ecedf23c (
  input  PR,
  input  J,
  input  Clock,
  input  K,
  input  CLR,
  output Q,
  output NOT_Q_56a63c63
);

  wire and_1_out, and_2_out, and_3_out, and_4_out, and_5_out, and_6_out, nand_1_out, nand_2_out, nand_3_out,
       nand_4_out, nand_5_out, nand_6_out, not_1_out, not_2_out;

  and and_1 (and_1_out, J, Clock);
  and and_2 (and_2_out, Clock, K);
  nand nand_1 (nand_1_out, and_1_out, NOT_Q_56a63c63);
  and and_3 (and_3_out, nand_3_out, nand_2_out);
  nand nand_2 (nand_2_out, Q, and_2_out);
  nand nand_3 (nand_3_out, PR, and_4_out);
  and and_4 (and_4_out, nand_1_out, nand_4_out);
  not not_1 (not_1_out, Clock);
  nand nand_4 (nand_4_out, and_3_out, not_2_out);
  not not_2 (not_2_out, CLR);
  nand nand_5 (nand_5_out, nand_3_out, not_1_out);
  nand nand_6 (nand_6_out, not_1_out, nand_4_out);
  and and_5 (and_5_out, PR, nand_5_out);
  and and_6 (and_6_out, nand_6_out, not_2_out);
  nand nand_7 (Q, and_5_out, NOT_Q_56a63c63);
  nand nand_8 (NOT_Q_56a63c63, Q, and_6_out);

  // Notes on the sheet:
  //   Q1
  //   ~Q1
  //   Set
  //   Reset
  //   Primeiro NAND
endmodule

module rs (
  input  pr,
  input  j,
  input  clock,
  input  k,
  input  cl,
  output q,
  output NOT_q_f302ee68
);

  wire and_1_out, and_2_out;

  and and_1 (and_1_out, j, NOT_q_f302ee68);
  and and_2 (and_2_out, q, k);
  S_R_Flip_Flop s_r_ff_1 (
    .S(and_1_out), .R(and_2_out), .clk(clock), .Q(q), .reset(cl), .Qn(NOT_q_f302ee68), .preset(pr));
endmodule

module CONTADOR_0_a_F_CRESCENTE_21d2d35d (
  input  On_Off_9958ac87,
  input  Clock,
  input  Clear
);

  wire flip_flop_jk_prclr_ecedf23c_1_q, flip_flop_jk_prclr_ecedf23c_2_q, flip_flop_jk_prclr_ecedf23c_3_q,
       flip_flop_jk_prclr_ecedf23c_4_q, l_7_seg_9e962840_1_a, l_7_seg_9e962840_1_b, l_7_seg_9e962840_1_c,
       l_7_seg_9e962840_1_d, l_7_seg_9e962840_1_e, l_7_seg_9e962840_1_f, l_7_seg_9e962840_1_g;

  FLIP_FLOP_JK_PRCLR_ecedf23c flip_flop_jk_prclr_ecedf23c_1 (
    .J(On_Off_9958ac87), .Clock(Clock), .K(On_Off_9958ac87), .CLR(Clear), .PR(1'b1),
    .Q(flip_flop_jk_prclr_ecedf23c_1_q));  // open: NOT_Q_56a63c63
  FLIP_FLOP_JK_PRCLR_ecedf23c flip_flop_jk_prclr_ecedf23c_2 (
    .J(On_Off_9958ac87), .Clock(flip_flop_jk_prclr_ecedf23c_1_q), .K(On_Off_9958ac87), .CLR(Clear),
    .PR(1'b1), .Q(flip_flop_jk_prclr_ecedf23c_2_q));  // open: NOT_Q_56a63c63
  FLIP_FLOP_JK_PRCLR_ecedf23c flip_flop_jk_prclr_ecedf23c_3 (
    .J(On_Off_9958ac87), .Clock(flip_flop_jk_prclr_ecedf23c_2_q), .K(On_Off_9958ac87), .CLR(Clear),
    .PR(1'b1), .Q(flip_flop_jk_prclr_ecedf23c_3_q));  // open: NOT_Q_56a63c63
  FLIP_FLOP_JK_PRCLR_ecedf23c flip_flop_jk_prclr_ecedf23c_4 (
    .J(On_Off_9958ac87), .Clock(flip_flop_jk_prclr_ecedf23c_3_q), .K(On_Off_9958ac87), .CLR(Clear),
    .PR(1'b1), .Q(flip_flop_jk_prclr_ecedf23c_4_q));  // open: NOT_Q_56a63c63
  L_7_seg_9e962840 l_7_seg_9e962840_1 (
    .in_1(flip_flop_jk_prclr_ecedf23c_4_q), .in_2(flip_flop_jk_prclr_ecedf23c_3_q),
    .in_3(flip_flop_jk_prclr_ecedf23c_2_q), .in_4(flip_flop_jk_prclr_ecedf23c_1_q), .a(l_7_seg_9e962840_1_a),
    .b(l_7_seg_9e962840_1_b), .c(l_7_seg_9e962840_1_c), .d(l_7_seg_9e962840_1_d), .e(l_7_seg_9e962840_1_e),
    .f(l_7_seg_9e962840_1_f), .g(l_7_seg_9e962840_1_g));
  _7_Segment_Display u_7_segment_display_1 (
    .g(l_7_seg_9e962840_1_g), .f(l_7_seg_9e962840_1_f), .a(l_7_seg_9e962840_1_a), .b(l_7_seg_9e962840_1_b),
    .e(l_7_seg_9e962840_1_e), .d(l_7_seg_9e962840_1_d), .c(l_7_seg_9e962840_1_c));  // open: dp

  // Notes on the sheet:
  //   na primeira execução, usar o clear pra começar a funcionar
endmodule

module CONTADOR_F_a_0_DECRESCENTE_09ffe537 (
  input  On_Off_9958ac87,
  input  Clock,
  input  Clear
);

  wire flip_flop_jk_prclr_ecedf23c_1_not_q_56a63c63, flip_flop_jk_prclr_ecedf23c_1_q,
       flip_flop_jk_prclr_ecedf23c_2_not_q_56a63c63, flip_flop_jk_prclr_ecedf23c_2_q,
       flip_flop_jk_prclr_ecedf23c_3_not_q_56a63c63, flip_flop_jk_prclr_ecedf23c_3_q,
       flip_flop_jk_prclr_ecedf23c_4_not_q_56a63c63, l_7_seg_9e962840_1_a, l_7_seg_9e962840_1_b,
       l_7_seg_9e962840_1_c, l_7_seg_9e962840_1_d, l_7_seg_9e962840_1_e, l_7_seg_9e962840_1_f,
       l_7_seg_9e962840_1_g;

  FLIP_FLOP_JK_PRCLR_ecedf23c flip_flop_jk_prclr_ecedf23c_1 (
    .J(On_Off_9958ac87), .Clock(Clock), .K(On_Off_9958ac87), .CLR(Clear), .PR(1'b1),
    .Q(flip_flop_jk_prclr_ecedf23c_1_q), .NOT_Q_56a63c63(flip_flop_jk_prclr_ecedf23c_1_not_q_56a63c63));
  FLIP_FLOP_JK_PRCLR_ecedf23c flip_flop_jk_prclr_ecedf23c_2 (
    .J(On_Off_9958ac87), .Clock(flip_flop_jk_prclr_ecedf23c_1_q), .K(On_Off_9958ac87), .CLR(Clear),
    .PR(1'b1), .Q(flip_flop_jk_prclr_ecedf23c_2_q),
    .NOT_Q_56a63c63(flip_flop_jk_prclr_ecedf23c_2_not_q_56a63c63));
  FLIP_FLOP_JK_PRCLR_ecedf23c flip_flop_jk_prclr_ecedf23c_3 (
    .J(On_Off_9958ac87), .Clock(flip_flop_jk_prclr_ecedf23c_2_q), .K(On_Off_9958ac87), .CLR(Clear),
    .PR(1'b1), .Q(flip_flop_jk_prclr_ecedf23c_3_q),
    .NOT_Q_56a63c63(flip_flop_jk_prclr_ecedf23c_3_not_q_56a63c63));
  FLIP_FLOP_JK_PRCLR_ecedf23c flip_flop_jk_prclr_ecedf23c_4 (
    .J(On_Off_9958ac87), .Clock(flip_flop_jk_prclr_ecedf23c_3_q), .K(On_Off_9958ac87), .CLR(Clear),
    .PR(1'b1), .NOT_Q_56a63c63(flip_flop_jk_prclr_ecedf23c_4_not_q_56a63c63));  // open: Q
  L_7_seg_9e962840 l_7_seg_9e962840_1 (
    .in_1(flip_flop_jk_prclr_ecedf23c_4_not_q_56a63c63), .in_2(flip_flop_jk_prclr_ecedf23c_3_not_q_56a63c63),
    .in_3(flip_flop_jk_prclr_ecedf23c_2_not_q_56a63c63), .in_4(flip_flop_jk_prclr_ecedf23c_1_not_q_56a63c63),
    .a(l_7_seg_9e962840_1_a), .b(l_7_seg_9e962840_1_b), .c(l_7_seg_9e962840_1_c), .d(l_7_seg_9e962840_1_d),
    .e(l_7_seg_9e962840_1_e), .f(l_7_seg_9e962840_1_f), .g(l_7_seg_9e962840_1_g));
  _7_Segment_Display u_7_segment_display_1 (
    .g(l_7_seg_9e962840_1_g), .f(l_7_seg_9e962840_1_f), .a(l_7_seg_9e962840_1_a), .b(l_7_seg_9e962840_1_b),
    .e(l_7_seg_9e962840_1_e), .d(l_7_seg_9e962840_1_d), .c(l_7_seg_9e962840_1_c));  // open: dp

  // Notes on the sheet:
  //   na primeira execução, usar o clear pra começar a funcionar
endmodule

module CONTADOR_0_a_9_CRESCENTE_c1de7d21 (
  input  Clock,
  input  On_Off_9958ac87,
  input  Clear
);

  wire and_1_out, and_2_out, flip_flop_jk_prclr_ecedf23c_1_q, flip_flop_jk_prclr_ecedf23c_2_q,
       flip_flop_jk_prclr_ecedf23c_3_q, flip_flop_jk_prclr_ecedf23c_4_q, l_7_seg_9e962840_1_a,
       l_7_seg_9e962840_1_b, l_7_seg_9e962840_1_c, l_7_seg_9e962840_1_d, l_7_seg_9e962840_1_e,
       l_7_seg_9e962840_1_f, l_7_seg_9e962840_1_g, or_1_out;

  and and_1 (and_1_out, On_Off_9958ac87, ~or_1_out);  // AND_Gate
  FLIP_FLOP_JK_PRCLR_ecedf23c flip_flop_jk_prclr_ecedf23c_1 (
    .J(and_1_out), .Clock(Clock), .K(and_1_out), .CLR(or_1_out), .PR(1'b1),
    .Q(flip_flop_jk_prclr_ecedf23c_1_q));  // open: NOT_Q_56a63c63
  FLIP_FLOP_JK_PRCLR_ecedf23c flip_flop_jk_prclr_ecedf23c_2 (
    .J(and_1_out), .Clock(flip_flop_jk_prclr_ecedf23c_1_q), .K(and_1_out), .CLR(or_1_out), .PR(1'b1),
    .Q(flip_flop_jk_prclr_ecedf23c_2_q));  // open: NOT_Q_56a63c63
  FLIP_FLOP_JK_PRCLR_ecedf23c flip_flop_jk_prclr_ecedf23c_3 (
    .J(and_1_out), .Clock(flip_flop_jk_prclr_ecedf23c_2_q), .K(and_1_out), .CLR(or_1_out), .PR(1'b1),
    .Q(flip_flop_jk_prclr_ecedf23c_3_q));  // open: NOT_Q_56a63c63
  or or_1 (or_1_out, and_2_out, Clear);
  FLIP_FLOP_JK_PRCLR_ecedf23c flip_flop_jk_prclr_ecedf23c_4 (
    .J(and_1_out), .Clock(flip_flop_jk_prclr_ecedf23c_3_q), .K(and_1_out), .CLR(or_1_out), .PR(1'b1),
    .Q(flip_flop_jk_prclr_ecedf23c_4_q));  // open: NOT_Q_56a63c63
  and and_2 (and_2_out, flip_flop_jk_prclr_ecedf23c_4_q, flip_flop_jk_prclr_ecedf23c_1_q);
  L_7_seg_9e962840 l_7_seg_9e962840_1 (
    .in_1(flip_flop_jk_prclr_ecedf23c_4_q), .in_2(flip_flop_jk_prclr_ecedf23c_3_q),
    .in_3(flip_flop_jk_prclr_ecedf23c_2_q), .in_4(flip_flop_jk_prclr_ecedf23c_1_q), .a(l_7_seg_9e962840_1_a),
    .b(l_7_seg_9e962840_1_b), .c(l_7_seg_9e962840_1_c), .d(l_7_seg_9e962840_1_d), .e(l_7_seg_9e962840_1_e),
    .f(l_7_seg_9e962840_1_f), .g(l_7_seg_9e962840_1_g));
  _7_Segment_Display u_7_segment_display_1 (
    .g(l_7_seg_9e962840_1_g), .f(l_7_seg_9e962840_1_f), .a(l_7_seg_9e962840_1_a), .b(l_7_seg_9e962840_1_b),
    .e(l_7_seg_9e962840_1_e), .d(l_7_seg_9e962840_1_d), .c(l_7_seg_9e962840_1_c));  // open: dp

  // Notes on the sheet:
  //   na primeira execução, usar o clear pra começar a funcionar
endmodule

module CONTADOR_9_a_0_DECRESCENTE_0351b7f5 (
  input  On_Off_9958ac87,
  input  Clock,
  input  Clear
);

  wire and_1_out, l_7_seg_9e962840_1_a, l_7_seg_9e962840_1_b, l_7_seg_9e962840_1_c, l_7_seg_9e962840_1_d,
       l_7_seg_9e962840_1_e, l_7_seg_9e962840_1_f, l_7_seg_9e962840_1_g, or_1_out, or_2_out, rs_1_q, rs_2_q,
       rs_3_q, rs_4_q;

  rs rs_1 (
    .j(On_Off_9958ac87), .clock(Clock), .k(On_Off_9958ac87), .pr(and_1_out), .cl(Clear), .q(rs_1_q));  // open: NOT_q_f302ee68
  rs rs_2 (
    .j(On_Off_9958ac87), .clock(rs_1_q), .k(On_Off_9958ac87), .cl(or_1_out), .q(rs_2_q));  // open: pr, NOT_q_f302ee68
  or or_1 (or_1_out, Clear, and_1_out);
  rs rs_3 (
    .j(On_Off_9958ac87), .clock(rs_2_q), .k(On_Off_9958ac87), .cl(or_2_out), .q(rs_3_q));  // open: pr, NOT_q_f302ee68
  or or_2 (or_2_out, Clear, and_1_out);
  rs rs_4 (
    .j(On_Off_9958ac87), .clock(rs_3_q), .k(On_Off_9958ac87), .pr(and_1_out), .cl(Clear), .q(rs_4_q));  // open: NOT_q_f302ee68
  and and_1 (and_1_out, ~rs_4_q, ~rs_3_q, ~rs_2_q, ~rs_1_q);  // AND_Gate
  L_7_seg_9e962840 l_7_seg_9e962840_1 (
    .in_1(rs_4_q), .in_2(rs_3_q), .in_3(rs_2_q), .in_4(rs_1_q), .a(l_7_seg_9e962840_1_a),
    .b(l_7_seg_9e962840_1_b), .c(l_7_seg_9e962840_1_c), .d(l_7_seg_9e962840_1_d), .e(l_7_seg_9e962840_1_e),
    .f(l_7_seg_9e962840_1_f), .g(l_7_seg_9e962840_1_g));
  _7_Segment_Display u_7_segment_display_1 (
    .g(l_7_seg_9e962840_1_g), .f(l_7_seg_9e962840_1_f), .a(l_7_seg_9e962840_1_a), .b(l_7_seg_9e962840_1_b),
    .e(l_7_seg_9e962840_1_e), .d(l_7_seg_9e962840_1_d), .c(l_7_seg_9e962840_1_c));  // open: dp
endmodule

module CONTADOR_0_a_N_CRESCENTE_c586b401 (
  input  On_Off_9958ac87,
  input  [3:0] in_2,
  input  Clock,
  input  Clear
);

  wire and_1_out, and_2_out, flip_flop_jk_prclr_ecedf23c_1_q, flip_flop_jk_prclr_ecedf23c_2_q,
       flip_flop_jk_prclr_ecedf23c_3_q, flip_flop_jk_prclr_ecedf23c_4_q, l_7_seg_9e962840_1_a,
       l_7_seg_9e962840_1_b, l_7_seg_9e962840_1_c, l_7_seg_9e962840_1_d, l_7_seg_9e962840_1_e,
       l_7_seg_9e962840_1_f, l_7_seg_9e962840_1_g, l_7_seg_9e962840_2_a, l_7_seg_9e962840_2_b,
       l_7_seg_9e962840_2_c, l_7_seg_9e962840_2_d, l_7_seg_9e962840_2_e, l_7_seg_9e962840_2_f,
       l_7_seg_9e962840_2_g, or_1_out, or_2_out, xnor_1_out, xnor_2_out, xnor_3_out, xnor_4_out;

  FLIP_FLOP_JK_PRCLR_ecedf23c flip_flop_jk_prclr_ecedf23c_1 (
    .J(On_Off_9958ac87), .Clock(Clock), .K(On_Off_9958ac87), .CLR(or_1_out), .PR(1'b1),
    .Q(flip_flop_jk_prclr_ecedf23c_1_q));  // open: NOT_Q_56a63c63
  FLIP_FLOP_JK_PRCLR_ecedf23c flip_flop_jk_prclr_ecedf23c_2 (
    .J(On_Off_9958ac87), .Clock(flip_flop_jk_prclr_ecedf23c_1_q), .K(On_Off_9958ac87), .CLR(or_1_out),
    .PR(1'b1), .Q(flip_flop_jk_prclr_ecedf23c_2_q));  // open: NOT_Q_56a63c63
  FLIP_FLOP_JK_PRCLR_ecedf23c flip_flop_jk_prclr_ecedf23c_3 (
    .J(On_Off_9958ac87), .Clock(flip_flop_jk_prclr_ecedf23c_2_q), .K(On_Off_9958ac87), .CLR(or_1_out),
    .PR(1'b1), .Q(flip_flop_jk_prclr_ecedf23c_3_q));  // open: NOT_Q_56a63c63
  FLIP_FLOP_JK_PRCLR_ecedf23c flip_flop_jk_prclr_ecedf23c_4 (
    .J(On_Off_9958ac87), .Clock(flip_flop_jk_prclr_ecedf23c_3_q), .K(On_Off_9958ac87), .CLR(or_1_out),
    .PR(1'b1), .Q(flip_flop_jk_prclr_ecedf23c_4_q));  // open: NOT_Q_56a63c63
  or or_1 (or_1_out, and_1_out, Clear);
  L_7_seg_9e962840 l_7_seg_9e962840_1 (
    .in_1(flip_flop_jk_prclr_ecedf23c_4_q), .in_2(flip_flop_jk_prclr_ecedf23c_3_q),
    .in_3(flip_flop_jk_prclr_ecedf23c_2_q), .in_4(flip_flop_jk_prclr_ecedf23c_1_q), .a(l_7_seg_9e962840_1_a),
    .b(l_7_seg_9e962840_1_b), .c(l_7_seg_9e962840_1_c), .d(l_7_seg_9e962840_1_d), .e(l_7_seg_9e962840_1_e),
    .f(l_7_seg_9e962840_1_f), .g(l_7_seg_9e962840_1_g));
  xnor xnor_1 (xnor_1_out, in_2[3], flip_flop_jk_prclr_ecedf23c_4_q);
  _7_Segment_Display u_7_segment_display_1 (
    .g(l_7_seg_9e962840_1_g), .f(l_7_seg_9e962840_1_f), .a(l_7_seg_9e962840_1_a), .b(l_7_seg_9e962840_1_b),
    .e(l_7_seg_9e962840_1_e), .d(l_7_seg_9e962840_1_d), .c(l_7_seg_9e962840_1_c));  // open: dp
  xnor xnor_2 (xnor_2_out, in_2[0], flip_flop_jk_prclr_ecedf23c_1_q);
  xnor xnor_3 (xnor_3_out, in_2[1], flip_flop_jk_prclr_ecedf23c_2_q);
  xnor xnor_4 (xnor_4_out, in_2[2], flip_flop_jk_prclr_ecedf23c_3_q);
  L_7_seg_9e962840 l_7_seg_9e962840_2 (
    .in_1(in_2[3]), .in_2(in_2[2]), .in_3(in_2[1]), .in_4(in_2[0]), .a(l_7_seg_9e962840_2_a),
    .b(l_7_seg_9e962840_2_b), .c(l_7_seg_9e962840_2_c), .d(l_7_seg_9e962840_2_d), .e(l_7_seg_9e962840_2_e),
    .f(l_7_seg_9e962840_2_f), .g(l_7_seg_9e962840_2_g));
  or or_2 (or_2_out, in_2[0], in_2[1], in_2[2], in_2[3]);
  and and_1 (and_1_out, or_2_out, and_2_out);
  and and_2 (and_2_out, xnor_2_out, xnor_3_out, xnor_4_out, xnor_1_out);
  _7_Segment_Display u_7_segment_display_2 (
    .g(l_7_seg_9e962840_2_g), .f(l_7_seg_9e962840_2_f), .a(l_7_seg_9e962840_2_a), .b(l_7_seg_9e962840_2_b),
    .e(l_7_seg_9e962840_2_e), .d(l_7_seg_9e962840_2_d), .c(l_7_seg_9e962840_2_c));  // open: dp

  // Notes on the sheet:
  //   na primeira execução, usar o clear pra começar a funcionar
  //   Selecionar Final
endmodule

module CONTADOR_N_a_0_DECRESCENTE_aadcdd3d (
  input  On_Off_9958ac87,
  input  Clock,
  input  Clear,
  input  [3:0] in_4
);

  wire and_1_out, and_2_out, and_3_out, and_4_out, and_5_out, l_7_seg_9e962840_1_a, l_7_seg_9e962840_1_b,
       l_7_seg_9e962840_1_c, l_7_seg_9e962840_1_d, l_7_seg_9e962840_1_e, l_7_seg_9e962840_1_f,
       l_7_seg_9e962840_1_g, l_7_seg_9e962840_2_a, l_7_seg_9e962840_2_b, l_7_seg_9e962840_2_c,
       l_7_seg_9e962840_2_d, l_7_seg_9e962840_2_e, l_7_seg_9e962840_2_f, l_7_seg_9e962840_2_g, rs_1_q,
       rs_2_q, rs_3_q, rs_4_q;

  not not_1 (On_Off_9958ac87, and_5_out);
  rs rs_1 (
    .j(On_Off_9958ac87), .clock(Clock), .k(On_Off_9958ac87), .pr(and_1_out), .cl(Clear), .q(rs_1_q));  // open: NOT_q_f302ee68
  and and_1 (and_1_out, in_4[0], and_5_out);
  rs rs_2 (
    .j(On_Off_9958ac87), .clock(rs_1_q), .k(On_Off_9958ac87), .pr(and_2_out), .cl(Clear), .q(rs_2_q));  // open: NOT_q_f302ee68
  and and_2 (and_2_out, in_4[1], and_5_out);
  rs rs_3 (
    .j(On_Off_9958ac87), .clock(rs_2_q), .k(On_Off_9958ac87), .pr(and_3_out), .cl(Clear), .q(rs_3_q));  // open: NOT_q_f302ee68
  and and_3 (and_3_out, in_4[2], and_5_out);
  rs rs_4 (
    .j(On_Off_9958ac87), .clock(rs_3_q), .k(On_Off_9958ac87), .pr(and_4_out), .cl(Clear), .q(rs_4_q));  // open: NOT_q_f302ee68
  and and_4 (and_4_out, in_4[3], and_5_out);
  and and_5 (and_5_out, ~rs_4_q, ~rs_3_q, ~rs_2_q, ~rs_1_q);  // AND_Gate
  L_7_seg_9e962840 l_7_seg_9e962840_1 (
    .in_1(in_4[3]), .in_2(in_4[2]), .in_3(in_4[1]), .in_4(in_4[0]), .a(l_7_seg_9e962840_1_a),
    .b(l_7_seg_9e962840_1_b), .c(l_7_seg_9e962840_1_c), .d(l_7_seg_9e962840_1_d), .e(l_7_seg_9e962840_1_e),
    .f(l_7_seg_9e962840_1_f), .g(l_7_seg_9e962840_1_g));
  L_7_seg_9e962840 l_7_seg_9e962840_2 (
    .in_1(rs_4_q), .in_2(rs_3_q), .in_3(rs_2_q), .in_4(rs_1_q), .a(l_7_seg_9e962840_2_a),
    .b(l_7_seg_9e962840_2_b), .c(l_7_seg_9e962840_2_c), .d(l_7_seg_9e962840_2_d), .e(l_7_seg_9e962840_2_e),
    .f(l_7_seg_9e962840_2_f), .g(l_7_seg_9e962840_2_g));
  _7_Segment_Display u_7_segment_display_1 (
    .g(l_7_seg_9e962840_1_g), .f(l_7_seg_9e962840_1_f), .a(l_7_seg_9e962840_1_a), .b(l_7_seg_9e962840_1_b),
    .e(l_7_seg_9e962840_1_e), .d(l_7_seg_9e962840_1_d), .c(l_7_seg_9e962840_1_c));  // open: dp
  _7_Segment_Display u_7_segment_display_2 (
    .g(l_7_seg_9e962840_2_g), .f(l_7_seg_9e962840_2_f), .a(l_7_seg_9e962840_2_a), .b(l_7_seg_9e962840_2_b),
    .e(l_7_seg_9e962840_2_e), .d(l_7_seg_9e962840_2_d), .c(l_7_seg_9e962840_2_c));  // open: dp

  // Notes on the sheet:
  //   Selecionar Inicio
endmodule

module CONTADOR_M_a_N_c9b2dcba (
  input  Clock,
  input  [3:0] in_2,
  input  On_Off_9958ac87,
  input  Clear,
  input  Crescente_Decrescente_77f37c88,
  input  [3:0] in_6
);

  wire and_1_out, and_2_out, and_3_out, and_4_out, and_5_out, and_6_out, and_7_out, and_8_out, and_9_out,
       and_10_out, and_11_out, and_12_out, l_7_seg_9e962840_1_a, l_7_seg_9e962840_1_b, l_7_seg_9e962840_1_c,
       l_7_seg_9e962840_1_d, l_7_seg_9e962840_1_e, l_7_seg_9e962840_1_f, l_7_seg_9e962840_1_g,
       l_7_seg_9e962840_2_a, l_7_seg_9e962840_2_b, l_7_seg_9e962840_2_c, l_7_seg_9e962840_2_d,
       l_7_seg_9e962840_2_e, l_7_seg_9e962840_2_f, l_7_seg_9e962840_2_g, l_7_seg_9e962840_3_a,
       l_7_seg_9e962840_3_b, l_7_seg_9e962840_3_c, l_7_seg_9e962840_3_d, l_7_seg_9e962840_3_e,
       l_7_seg_9e962840_3_f, l_7_seg_9e962840_3_g, not_1_out, or_1_out, or_2_out, or_3_out, or_4_out,
       or_5_out, rs_1_not_q_f302ee68, rs_1_q, rs_2_not_q_f302ee68, rs_2_q, rs_3_not_q_f302ee68, rs_3_q,
       rs_4_q, xnor_1_out, xnor_2_out, xnor_3_out, xnor_4_out;

  and and_1 (and_1_out, in_6[0], or_4_out);
  rs rs_1 (
    .j(On_Off_9958ac87), .clock(Clock), .k(On_Off_9958ac87), .pr(and_1_out), .cl(or_4_out), .q(rs_1_q),
    .NOT_q_f302ee68(rs_1_not_q_f302ee68));
  not not_1 (not_1_out, Crescente_Decrescente_77f37c88);
  and and_2 (and_2_out, Crescente_Decrescente_77f37c88, rs_1_q);
  or or_1 (or_1_out, and_2_out, and_3_out);
  and and_3 (and_3_out, rs_1_not_q_f302ee68, not_1_out);
  and and_4 (and_4_out, in_6[1], or_4_out);
  rs rs_2 (
    .j(On_Off_9958ac87), .clock(or_1_out), .k(On_Off_9958ac87), .pr(and_4_out), .cl(or_4_out), .q(rs_2_q),
    .NOT_q_f302ee68(rs_2_not_q_f302ee68));
  L_7_seg_9e962840 l_7_seg_9e962840_1 (
    .in_1(in_6[3]), .in_2(in_6[2]), .in_3(in_6[1]), .in_4(in_6[0]), .a(l_7_seg_9e962840_1_a),
    .b(l_7_seg_9e962840_1_b), .c(l_7_seg_9e962840_1_c), .d(l_7_seg_9e962840_1_d), .e(l_7_seg_9e962840_1_e),
    .f(l_7_seg_9e962840_1_f), .g(l_7_seg_9e962840_1_g));
  and and_5 (and_5_out, Crescente_Decrescente_77f37c88, rs_2_q);
  or or_2 (or_2_out, and_5_out, and_6_out);
  and and_6 (and_6_out, rs_2_not_q_f302ee68, not_1_out);
  and and_7 (and_7_out, in_6[2], or_4_out);
  rs rs_3 (
    .j(On_Off_9958ac87), .clock(or_2_out), .k(On_Off_9958ac87), .pr(and_7_out), .cl(or_4_out), .q(rs_3_q),
    .NOT_q_f302ee68(rs_3_not_q_f302ee68));
  _7_Segment_Display u_7_segment_display_1 (
    .g(l_7_seg_9e962840_1_g), .f(l_7_seg_9e962840_1_f), .a(l_7_seg_9e962840_1_a), .b(l_7_seg_9e962840_1_b),
    .e(l_7_seg_9e962840_1_e), .d(l_7_seg_9e962840_1_d), .c(l_7_seg_9e962840_1_c));  // open: dp
  and and_8 (and_8_out, Crescente_Decrescente_77f37c88, rs_3_q);
  or or_3 (or_3_out, and_8_out, and_9_out);
  and and_9 (and_9_out, rs_3_not_q_f302ee68, not_1_out);
  and and_10 (and_10_out, in_6[3], or_4_out);
  rs rs_4 (
    .j(On_Off_9958ac87), .clock(or_3_out), .k(On_Off_9958ac87), .pr(and_10_out), .cl(or_4_out), .q(rs_4_q));  // open: NOT_q_f302ee68
  or or_4 (or_4_out, and_11_out, Clear);
  L_7_seg_9e962840 l_7_seg_9e962840_2 (
    .in_1(rs_4_q), .in_2(rs_3_q), .in_3(rs_2_q), .in_4(rs_1_q), .a(l_7_seg_9e962840_2_a),
    .b(l_7_seg_9e962840_2_b), .c(l_7_seg_9e962840_2_c), .d(l_7_seg_9e962840_2_d), .e(l_7_seg_9e962840_2_e),
    .f(l_7_seg_9e962840_2_f), .g(l_7_seg_9e962840_2_g));
  xnor xnor_1 (xnor_1_out, in_2[2], rs_3_q);
  xnor xnor_2 (xnor_2_out, in_2[3], rs_4_q);
  _7_Segment_Display u_7_segment_display_2 (
    .g(l_7_seg_9e962840_2_g), .f(l_7_seg_9e962840_2_f), .a(l_7_seg_9e962840_2_a), .b(l_7_seg_9e962840_2_b),
    .e(l_7_seg_9e962840_2_e), .d(l_7_seg_9e962840_2_d), .c(l_7_seg_9e962840_2_c));  // open: dp
  xnor xnor_3 (xnor_3_out, in_2[0], rs_1_q);
  xnor xnor_4 (xnor_4_out, in_2[1], rs_2_q);
  L_7_seg_9e962840 l_7_seg_9e962840_3 (
    .in_1(in_2[3]), .in_2(in_2[2]), .in_3(in_2[1]), .in_4(in_2[0]), .a(l_7_seg_9e962840_3_a),
    .b(l_7_seg_9e962840_3_b), .c(l_7_seg_9e962840_3_c), .d(l_7_seg_9e962840_3_d), .e(l_7_seg_9e962840_3_e),
    .f(l_7_seg_9e962840_3_f), .g(l_7_seg_9e962840_3_g));
  or or_5 (or_5_out, in_2[0], in_2[1], in_2[2], in_2[3]);
  and and_11 (and_11_out, or_5_out, and_12_out);
  and and_12 (and_12_out, xnor_3_out, xnor_4_out, xnor_1_out, xnor_2_out);
  _7_Segment_Display u_7_segment_display_3 (
    .g(l_7_seg_9e962840_3_g), .f(l_7_seg_9e962840_3_f), .a(l_7_seg_9e962840_3_a), .b(l_7_seg_9e962840_3_b),
    .e(l_7_seg_9e962840_3_e), .d(l_7_seg_9e962840_3_d), .c(l_7_seg_9e962840_3_c));  // open: dp

  // Notes on the sheet:
  //   Selecionar Inicio
  //   Selecionar Final
endmodule

module L_7_seg_9e962840 (
  input  in_1,
  input  in_2,
  input  in_3,
  input  in_4,
  output a,
  output b,
  output c,
  output d,
  output e,
  output f,
  output g
);

  wire and_1_out, and_2_out, and_3_out, and_4_out, and_5_out, and_6_out, and_7_out, and_8_out, and_9_out,
       and_10_out, and_11_out, and_12_out, and_13_out, and_14_out, and_15_out, and_16_out, and_17_out,
       and_18_out, and_19_out, and_20_out, and_21_out, and_22_out, and_23_out, and_24_out, and_25_out,
       and_26_out, and_27_out, and_28_out, and_29_out, and_30_out, and_31_out, and_32_out, and_33_out,
       and_34_out, and_35_out, and_36_out, and_37_out, and_38_out, and_39_out, and_40_out, and_41_out,
       and_42_out, and_43_out, and_44_out, and_45_out, and_46_out, not_1_out, not_2_out, not_3_out,
       not_4_out, not_5_out, not_6_out, not_7_out, not_8_out, not_9_out, not_10_out, not_11_out, not_12_out,
       not_13_out, not_14_out, not_15_out, not_16_out, not_17_out, not_18_out, not_19_out, not_20_out,
       not_21_out, not_22_out, not_23_out, not_24_out, not_25_out, not_26_out, not_27_out, not_28_out,
       not_29_out, not_30_out, not_31_out, not_32_out, not_33_out, not_34_out, not_35_out, not_36_out,
       not_37_out, not_38_out, not_39_out, not_40_out, not_41_out, not_42_out, not_43_out, or_1_out,
       or_2_out, or_3_out, or_4_out, or_5_out, or_6_out, or_7_out, or_8_out, or_9_out, or_10_out, or_12_out,
       or_13_out, or_14_out, or_15_out, or_16_out, or_17_out, or_18_out, or_20_out, or_21_out, or_22_out,
       or_23_out;

  not not_1 (not_1_out, in_2);
  not not_2 (not_2_out, in_4);
  not not_3 (not_3_out, in_1);
  not not_4 (not_4_out, in_1);
  and and_1 (and_1_out, in_1, not_5_out);
  not not_5 (not_5_out, in_2);
  not not_6 (not_6_out, in_3);
  not not_7 (not_7_out, in_1);
  not not_8 (not_8_out, in_2);
  not not_9 (not_9_out, in_1);
  and and_2 (and_2_out, not_9_out, not_10_out);
  not not_10 (not_10_out, in_3);
  not not_11 (not_11_out, in_4);
  not not_12 (not_12_out, in_1);
  not not_13 (not_13_out, in_3);
  not not_14 (not_14_out, in_1);
  and and_3 (and_3_out, not_14_out, not_15_out);
  not not_15 (not_15_out, in_3);
  not not_16 (not_16_out, in_1);
  and and_4 (and_4_out, not_16_out, in_4);
  not not_17 (not_17_out, in_3);
  not not_18 (not_18_out, in_1);
  not not_19 (not_19_out, in_2);
  not not_20 (not_20_out, in_1);
  and and_5 (and_5_out, not_20_out, not_21_out);
  not not_21 (not_21_out, in_2);
  not not_22 (not_22_out, in_4);
  not not_23 (not_23_out, in_2);
  and and_6 (and_6_out, not_23_out, in_3);
  not not_24 (not_24_out, in_3);
  not not_25 (not_25_out, in_2);
  and and_7 (and_7_out, not_25_out, not_26_out);
  not not_26 (not_26_out, in_4);
  and and_8 (and_8_out, in_3, not_27_out);
  not not_27 (not_27_out, in_4);
  and and_9 (and_9_out, in_1, in_3);
  and and_10 (and_10_out, in_1, in_2);
  not not_28 (not_28_out, in_3);
  not not_29 (not_29_out, in_4);
  not not_30 (not_30_out, in_1);
  and and_11 (and_11_out, not_30_out, in_2);
  not not_31 (not_31_out, in_3);
  not not_32 (not_32_out, in_2);
  and and_12 (and_12_out, not_32_out, in_3);
  and and_13 (and_13_out, in_3, not_33_out);
  not not_33 (not_33_out, in_4);
  not not_34 (not_34_out, in_1);
  and and_14 (and_14_out, not_34_out, in_2);
  not not_35 (not_35_out, in_3);
  not not_36 (not_36_out, in_2);
  and and_15 (and_15_out, not_1_out, not_2_out);
  and and_16 (and_16_out, not_3_out, in_3);
  and and_17 (and_17_out, not_4_out, in_2);
  and and_18 (and_18_out, in_2, in_3);
  and and_19 (and_19_out, and_1_out, not_6_out);
  not not_37 (not_37_out, in_4);
  and and_20 (and_20_out, not_7_out, not_8_out);
  and and_21 (and_21_out, and_2_out, not_11_out);
  not not_38 (not_38_out, in_2);
  not not_39 (not_39_out, in_4);
  and and_22 (and_22_out, not_12_out, in_3);
  and and_23 (and_23_out, in_1, not_13_out);
  or or_1 (or_1_out, and_3_out, and_4_out);
  and and_24 (and_24_out, not_17_out, in_4);
  and and_25 (and_25_out, not_18_out, in_2);
  and and_26 (and_26_out, in_1, not_19_out);
  and and_27 (and_27_out, and_5_out, not_22_out);
  and and_28 (and_28_out, and_6_out, in_4);
  and and_29 (and_29_out, in_2, not_24_out);
  and and_30 (and_30_out, in_2, in_3);
  not not_40 (not_40_out, in_4);
  not not_41 (not_41_out, in_3);
  or or_2 (or_2_out, and_7_out, and_8_out);
  or or_3 (or_3_out, and_9_out, and_10_out);
  and and_31 (and_31_out, not_28_out, not_29_out);
  and and_32 (and_32_out, and_11_out, not_31_out);
  not not_42 (not_42_out, in_4);
  not not_43 (not_43_out, in_2);
  or or_4 (or_4_out, and_12_out, and_13_out);
  and and_33 (and_33_out, and_14_out, not_35_out);
  and and_34 (and_34_out, in_1, not_36_out);
  and and_35 (and_35_out, in_1, in_4);
  or or_5 (or_5_out, and_15_out, and_16_out);
  and and_36 (and_36_out, and_17_out, in_4);
  or or_6 (or_6_out, and_18_out, and_19_out);
  and and_37 (and_37_out, in_1, not_37_out);
  or or_7 (or_7_out, and_20_out, and_21_out);
  and and_38 (and_38_out, not_38_out, not_39_out);
  and and_39 (and_39_out, and_22_out, in_4);
  and and_40 (and_40_out, and_23_out, in_4);
  or or_8 (or_8_out, or_1_out, and_24_out);
  or or_9 (or_9_out, and_25_out, and_26_out);
  or or_10 (or_10_out, and_27_out, and_28_out);
  and and_41 (and_41_out, and_29_out, in_4);
  and and_42 (and_42_out, and_30_out, not_40_out);
  and and_43 (and_43_out, in_1, not_41_out);
  or or_11 (e, or_2_out, or_3_out);
  or or_12 (or_12_out, and_31_out, and_32_out);
  and and_44 (and_44_out, in_2, not_42_out);
  and and_45 (and_45_out, in_1, not_43_out);
  and and_46 (and_46_out, in_1, in_3);
  or or_13 (or_13_out, or_4_out, and_33_out);
  or or_14 (or_14_out, and_34_out, and_35_out);
  or or_15 (or_15_out, or_5_out, and_36_out);
  or or_16 (or_16_out, or_6_out, and_37_out);
  or or_17 (or_17_out, or_7_out, and_38_out);
  or or_18 (or_18_out, and_39_out, and_40_out);
  or or_19 (c, or_8_out, or_9_out);
  or or_20 (or_20_out, or_10_out, and_41_out);
  or or_21 (or_21_out, and_42_out, and_43_out);
  or or_22 (or_22_out, or_12_out, and_44_out);
  or or_23 (or_23_out, and_45_out, and_46_out);
  or or_24 (g, or_13_out, or_14_out);
  or or_25 (a, or_15_out, or_16_out);
  or or_26 (b, or_17_out, or_18_out);
  or or_27 (d, or_20_out, or_21_out);
  or or_28 (f, or_22_out, or_23_out);
endmodule
