// Logisim project Contadores Sincronos.circ as structural Verilog
module main (
  input  in_1
);

  wire clock_1_out, n0_a_9_1_j0, n0_a_9_1_j1, n0_a_9_1_j2, n0_a_9_1_j3, n0_a_9_1_k0, n0_a_9_1_k1,
       n0_a_9_1_k2, n0_a_9_1_k3;
  wire [3:0] j_k_ff_4_q;

  Clock clock_1 (.out(clock_1_out));
  J_K_Flip_Flop j_k_ff_1 (
    .J(n0_a_9_1_j3), .clk(clock_1_out), .K(n0_a_9_1_k3), .Q(j_k_ff_4_q[3]), .reset(in_1));  // open: Qn, preset, en
  J_K_Flip_Flop j_k_ff_2 (
    .J(n0_a_9_1_k2), .clk(clock_1_out), .K(n0_a_9_1_j2), .Q(j_k_ff_4_q[2]), .reset(in_1));  // open: Qn, preset, en
  J_K_Flip_Flop j_k_ff_3 (
    .J(n0_a_9_1_j1), .clk(clock_1_out), .K(n0_a_9_1_k1), .Q(j_k_ff_4_q[1]), .reset(in_1));  // open: Qn, preset, en
  J_K_Flip_Flop j_k_ff_4 (
    .J(n0_a_9_1_j0), .clk(clock_1_out), .K(n0_a_9_1_k0), .Q(j_k_ff_4_q[0]), .reset(in_1));  // open: Qn, preset, en
  _0_a_9 u_0_a_9_1 (
    .Q3(j_k_ff_4_q[3]), .Q2(j_k_ff_4_q[2]), .Q1(j_k_ff_4_q[1]), .Q0(j_k_ff_4_q[0]), .J3(n0_a_9_1_j3),
    .K3(n0_a_9_1_k3), .J2(n0_a_9_1_j2), .K2(n0_a_9_1_k2), .J1(n0_a_9_1_j1), .K1(n0_a_9_1_k1),
    .J0(n0_a_9_1_j0), .K0(n0_a_9_1_k0));
  Hex_Digit_Display hex_digit_display_1 (.value(j_k_ff_4_q));  // open: dp
endmodule

module _0_a_F (
  input  Q3,
  input  Q2,
  input  Q1,
  input  Q0,
  output J3,
  output K3,
  output J2,
  output K2,
  output J1,
  output K1,
  output J0,
  output K0
);

  wire and_1_out;

  and and_1 (and_1_out, Q2, Q1, Q0);
  and and_2 (K3, Q2, Q1, Q0);
  and and_3 (J2, Q1, Q0);
  and and_4 (K2, Q1, Q0);
  or or_1 (J3, and_1_out, Q3);

  assign J0 = 1'b1;
  assign J1 = Q0;
  assign K0 = 1'b1;
  assign K1 = Q0;
endmodule

module _0_a_9 (
  input  Q3,
  input  Q2,
  input  Q1,
  input  Q0,
  output J3,
  output K3,
  output J2,
  output K2,
  output J1,
  output K1,
  output J0,
  output K0
);

  wire not_1_out;

  and and_1 (J3, Q2, Q1, Q0);
  and and_2 (J2, Q1, Q0);
  and and_3 (K2, Q1, Q0);
  not not_1 (not_1_out, Q3);
  and and_4 (J1, not_1_out, Q0);

  assign J0 = 1'b1;
  assign K0 = 1'b1;
  assign K1 = Q0;
  assign K3 = Q0;
endmodule

module Contador_0_a_N (
  input  Seletor_Final,
  input  in_2,
  input  in_3,
  input  in_4,
  input  in_5
);

  wire clock_1_out, n0_a_9_1_j0, n0_a_9_1_j1, n0_a_9_1_j2, n0_a_9_1_j3, n0_a_9_1_k0, n0_a_9_1_k1,
       n0_a_9_1_k2, n0_a_9_1_k3, or_1_out, thebarragem_1_sel;
  wire [3:0] j_k_ff_4_q;

  Clock clock_1 (.out(clock_1_out));
  J_K_Flip_Flop j_k_ff_1 (
    .J(n0_a_9_1_j3), .clk(clock_1_out), .K(n0_a_9_1_k3), .Q(j_k_ff_4_q[3]), .reset(or_1_out));  // open: Qn, preset, en
  J_K_Flip_Flop j_k_ff_2 (
    .J(n0_a_9_1_k2), .clk(clock_1_out), .K(n0_a_9_1_j2), .Q(j_k_ff_4_q[2]), .reset(or_1_out));  // open: Qn, preset, en
  J_K_Flip_Flop j_k_ff_3 (
    .J(n0_a_9_1_j1), .clk(clock_1_out), .K(n0_a_9_1_k1), .Q(j_k_ff_4_q[1]), .reset(or_1_out));  // open: Qn, preset, en
  J_K_Flip_Flop j_k_ff_4 (
    .J(n0_a_9_1_j0), .clk(clock_1_out), .K(n0_a_9_1_k0), .Q(j_k_ff_4_q[0]), .reset(or_1_out));  // open: Qn, preset, en
  _0_a_9 u_0_a_9_1 (
    .Q3(j_k_ff_4_q[3]), .Q2(j_k_ff_4_q[2]), .Q1(j_k_ff_4_q[1]), .Q0(j_k_ff_4_q[0]), .J3(n0_a_9_1_j3),
    .K3(n0_a_9_1_k3), .J2(n0_a_9_1_j2), .K2(n0_a_9_1_k2), .J1(n0_a_9_1_j1), .K1(n0_a_9_1_k1),
    .J0(n0_a_9_1_j0), .K0(n0_a_9_1_k0));
  Hex_Digit_Display hex_digit_display_1 (.value(j_k_ff_4_q));  // open: dp
  TheBarragem thebarragem_1 (
    .Q0(j_k_ff_4_q[0]), .Q1(j_k_ff_4_q[1]), .Q2(j_k_ff_4_q[2]), .Q3(j_k_ff_4_q[3]), .s3(in_4), .s2(in_3),
    .s1(in_2), .s0(Seletor_Final), .sel(thebarragem_1_sel));
  or or_1 (or_1_out, thebarragem_1_sel, in_5);
  Hex_Digit_Display hex_digit_display_2 (.value({in_4, in_3, in_2, Seletor_Final}));  // open: dp
endmodule

module TheBarragem (
  input  s3,
  input  s2,
  input  s1,
  input  s0,
  input  Q0,
  input  Q1,
  input  Q2,
  input  Q3,
  output sel
);

  wire xnor_1_out, xnor_2_out, xnor_3_out, xnor_4_out;

  xnor xnor_1 (xnor_1_out, s2, Q2);
  xnor xnor_2 (xnor_2_out, s3, Q3);
  xnor xnor_3 (xnor_3_out, s0, Q0);
  xnor xnor_4 (xnor_4_out, s1, Q1);
  and and_1 (sel, xnor_3_out, xnor_4_out, xnor_1_out, xnor_2_out);
endmodule
