// Logisim project FlipFlop.circ as structural Verilog
module FlipFlop_JK_PRCLR (
  input  PR,
  input  J,
  input  Clock,
  input  K,
  input  CLR,
  output Q,
  output nQ
);

  wire and_1_out, and_2_out, and_3_out, and_4_out, and_5_out, and_6_out, nand_1_out, nand_2_out, nand_3_out,
       nand_4_out, nand_5_out, nand_6_out, not_1_out;

  and and_1 (and_1_out, J, Clock);
  and and_2 (and_2_out, Clock, K);
  nand nand_1 (nand_1_out, and_1_out, nQ);
  nand nand_2 (nand_2_out, Q, and_2_out);
  nand nand_3 (nand_3_out, PR, and_3_out);
  and and_3 (and_3_out, nand_1_out, nand_4_out);
  not not_1 (not_1_out, Clock);
  and and_4 (and_4_out, nand_3_out, nand_2_out);
  nand nand_4 (nand_4_out, and_4_out, CLR);
  nand nand_5 (nand_5_out, nand_3_out, not_1_out);
  nand nand_6 (nand_6_out, not_1_out, nand_4_out);
  and and_5 (and_5_out, PR, nand_5_out);
  and and_6 (and_6_out, nand_6_out, CLR);
  nand nand_7 (Q, and_5_out, nQ);
  nand nand_8 (nQ, Q, and_6_out);

  // Notes on the sheet:
  //   Q1
  //   ~Q1
  //   Set
  //   Reset
  //   Primeiro NAND
endmodule

module FLIP_FLOP_T (
  input  T,
  input  PR,
  input  CLOCK,
  input  CLR,
  output out_5,
  output out_6
);

  FlipFlop_JK_PRCLR flipflop_jk_prclr_1 (.J(T), .Clock(CLOCK), .K(T), .Q(out_5), .nQ(out_6), .PR(PR), .CLR(CLR));
endmodule

module FLIP_FLOP_D (
  input  D,
  input  PR,
  input  CLOCK,
  input  CL,
  output Q,
  output nQ
);

  wire not_1_out;

  not not_1 (not_1_out, D);
  FlipFlop_JK_PRCLR flipflop_jk_prclr_1 (.J(D), .Clock(CLOCK), .K(not_1_out), .Q(Q), .nQ(nQ), .PR(PR), .CLR(CL));
endmodule

module aaaa (
  input  in_1,
  input  in_2,
  input  in_3,
  input  in_4,
  input  in_5,
  input  in_6,
  output out_7,
  output out_8,
  output out_9,
  output out_10
);

  wire clock_1_out, not_1_out, not_2_out, not_3_out, not_4_out, not_5_out;

  not not_1 (not_1_out, in_2);
  not not_2 (not_2_out, in_3);
  Clock clock_1 (.out(clock_1_out));
  FLIP_FLOP_D flip_flop_d_1 (.CLOCK(clock_1_out), .Q(out_7), .D(in_1), .PR(not_2_out), .CL(not_1_out));  // open: nQ
  FLIP_FLOP_D flip_flop_d_2 (.CLOCK(clock_1_out), .Q(out_8), .D(out_7), .PR(not_3_out), .CL(not_1_out));  // open: nQ
  not not_3 (not_3_out, in_4);
  FLIP_FLOP_D flip_flop_d_3 (.CLOCK(clock_1_out), .Q(out_9), .D(out_8), .PR(not_4_out), .CL(not_1_out));  // open: nQ
  not not_4 (not_4_out, in_5);
  FLIP_FLOP_D flip_flop_d_4 (.CLOCK(clock_1_out), .Q(out_10), .D(out_9), .PR(not_5_out), .CL(not_1_out));  // open: nQ
  not not_5 (not_5_out, in_6);
endmodule
